# Fritzing sketch ESP06 (saved by Fritzing 0.9.3b)
circuit board: 3.94488cm x 3.32842cm
breadboards: 1

parts:
  C1 = Capacitor Polarized [package=cpol-radial-100uf-25v]
  hc-sr1 = hc-sr04
  DS2 = DS18B20 1-Wire Temperature Sensor [part_number=DS18B20]
  DS1 = DS18B20 1-Wire Temperature Sensor [part_number=DS18B20]
  J1 = female pin header, 2 pins [form="♀ (female)" part_number="5V IN"]
  R4 = Resistor [tolerance=±5% resistance=2.2k package="1206 [SMD]"]
  R2 = Resistor [tolerance=±5% resistance=4.7k package="1206 [SMD]"]
  R1 = Resistor [tolerance=±5% resistance=4.7k package="1206 [SMD]"]
  IC1 = Voltage Regulator LM1117 [part_number=TS1117BCW package=sot223]
  J5 = female pin header, 3 pins [form="♀ (female)"]
  J6 = female pin header, 6 pins [form="♀ (female)"]
  J3 = male pin header, 3 pins [form="♂ (male)" part_number="rst / flash"]
  C3 = Capacitor [package=1206]
  C2 = Capacitor [package=1206]
  R6 = Resistor [tolerance=±5% resistance=10k package="1206 [SMD]"]
  R3 = Resistor [tolerance=±5% resistance=4.7k package="1206 [SMD]"]
  R5 = Resistor [tolerance=±5% resistance=4.7k package="1206 [SMD]"]
  U6 = ESP-12F (ESP8266 WiFi Module) [part_number=ESP8266]

nets:
  3.3V: C1.+, DS2.VDD, DS1.VDD, R4.Pin_0, R2.Pin_0, R1.Pin_0, IC1.OUT, J5.pin3, J6.pin6, C3.1, R3.Pin_0, U6.VCC, U6.EN
  GND: C1.-, hc-sr1.GND, DS2.GND, DS1.GND, J1.pin2, IC1.ADJ, J5.pin1, J6.pin1, J3.pin2, C3.2, C2.2, R6.Pin_0, U6.GND, U6.GPIO15
  5V: hc-sr1.VCC, J1.pin1, IC1.IN, J6.pin4, C2.1
  GPIO3 -> TRIG: hc-sr1.Trig, J6.pin3, U6.TXD0
  GPIO1 -> ECHO: hc-sr1.Echo, J6.pin2, R5.Pin_1
  ONE WIRE: DS2.DQ, DS1.DQ, R4.Pin_1, J5.pin2, J6.pin5, U6.GPIO5
  N1: R2.Pin_1, U6.GPIO2
  N2: R1.Pin_1, J3.pin1, U6.RST
  N3: J3.pin3, R3.Pin_1, U6.GPIO0
  N4: R6.Pin_1, R5.Pin_0, U6.RXD0

notes:
  ESP 6
  5V
  echo
  trig
  GND
  3.3V
  1w
  rst
  /  \
  rev2

custom parts:
  ESP-12F (ESP8266 WiFi Module): WiFi Module based on the ESP8266 with onboard PCB antenna and UART communications
